// Logisim project trabalho2_arq.circ as structural Verilog: 8 circuits, main circuit main
module main (
);

  wire button_1_out, mux_IMM, mux_JR, mux_PCIMM, mux_PCRb, write_Breg, write_mem;
  wire [1:0] decodificador_1_ra, decodificador_1_rb, mux_Data;
  wire [3:0] decodificador_1_imm, decodificador_1_opcode, op_ula;
  wire [7:0] addr, d, data_Mem, data_RA, imm, multiplexer_1_out, pc_1_instruction, ula_1_data;

  PC pc_1 (
    .addr(addr), .d(d), .w(write_mem), .Rb(addr), .IMM(imm), .mux_PCRb(mux_PCRb), .mux_PCIMM(mux_PCIMM),
    .mux_JR(mux_JR), .Instruction(pc_1_instruction), .data(data_Mem));
  // Probe on data_Mem
  // Probe on pc_1_instruction
  Decodificador decodificador_1 (
    .Instruction(pc_1_instruction), .Rb(decodificador_1_rb), .Ra(decodificador_1_ra),
    .Opcode(decodificador_1_opcode), .IMM(decodificador_1_imm));
  Button button_1 (.out(button_1_out));
  assign imm = {{4{decodificador_1_imm[3]}}, decodificador_1_imm};  // Bit_Extender bit_extender_1
  Unidade_Controle unidade_controle_1 (
    .opcode(decodificador_1_opcode), .op_ula(op_ula), .write_Breg(write_Breg), .write_mem(write_mem),
    .mux_PCIMM(mux_PCIMM), .mux_IMM(mux_IMM), .mux_PCRb(mux_PCRb), .mux_Data(mux_Data), .mux_JR(mux_JR));
  Banco_Reg banco_reg_1 (
    .Write(write_Breg), .Ra(decodificador_1_ra), .Data(d), .Rb(decodificador_1_rb),
    .Reset_Breg(button_1_out), .Saida_A(data_RA), .Saida_B(addr));
  // Probe on imm
  // Probe on addr
  Multiplexer #(.width(8)) multiplexer_1 (.in0(addr), .in1(imm), .out(multiplexer_1_out), .sel(mux_IMM));
  ULA ula_1 (.A(data_RA), .B(multiplexer_1_out), .op_ula(op_ula), .Data(ula_1_data));
  Multiplexer #(.select(2), .width(8)) multiplexer_2 (
    .in0(ula_1_data), .in1(data_RA), .in2(data_Mem), .out(d), .sel(mux_Data));  // open: in3

  // Other names for the same wires on the sheet: B[7:0] = addr
endmodule

module PC (
  input  [7:0] addr,
  input  [7:0] d,
  input  w,
  input  [7:0] Rb,
  input  [7:0] IMM,
  input  mux_PCRb,
  input  mux_PCIMM,
  input  mux_JR,
  output [7:0] Instruction,
  output [7:0] data
);

  wire and_1_out, bit_extender_1_out, clock_1_out, multiplexer_3_out, not_1_out, reset_out;
  wire [7:0] adder_1_out, multiplexer_1_out, nor_1_out, PC, register_1_q;

  Register register_1 (.D(PC), .en(1'b1), .clk(clock_1_out), .Q(register_1_q), .clr(reset_out));
  Clock #(.highDuration(2), .lowDuration(2)) clock_1 (.out(clock_1_out));
  Button reset (.out(reset_out));
  Multiplexer #(.width(8)) multiplexer_1 (.in0(8'h1), .in1(IMM), .out(multiplexer_1_out), .sel(mux_PCIMM));
  // Probe on register_1_q
  Adder adder_1 (.a(register_1_q), .b(multiplexer_1_out), .out(adder_1_out));  // open: cin, cout
  assign nor_1_out = ~(d | {8{1'b0}});  // NOR_Gate nor_1, 8 bits wide
  Multiplexer #(.width(8)) multiplexer_2 (.in0(adder_1_out), .in1(Rb), .out(PC), .sel(multiplexer_3_out));
  Multiplexer multiplexer_3 (.in0(and_1_out), .in1(1'b1), .out(multiplexer_3_out), .sel(mux_JR));
  Bit_Extender #(.out_width(1)) bit_extender_1 (.in(nor_1_out), .out(bit_extender_1_out));
  and and_1 (and_1_out, not_1_out, mux_PCRb);
  not not_1 (not_1_out, bit_extender_1_out);
  dual_port_ram dual_port_ram_1 (.addr(addr), .pc(register_1_q), .d(d), .w(w), .instr(Instruction), .data(data));
endmodule

module Decodificador (
  input  [7:0] Instruction,
  output [1:0] Rb,
  output [1:0] Ra,
  output [3:0] Opcode,
  output [3:0] IMM
);

  wire comparator_1_eq;

  Comparator #(.width(4)) comparator_1 (.a(Instruction[7:4]), .b(4'b0100), .eq(comparator_1_eq));  // open: gt, lt
  Multiplexer #(.width(2)) multiplexer_1 (.in0(Instruction[3:2]), .in1(2'b00), .out(Ra), .sel(comparator_1_eq));

  assign IMM = Instruction[3:0];
  assign Opcode = Instruction[7:4];
  assign Rb = Instruction[1:0];
endmodule

module new_ram (
  output [7:0] out_1,
  output [7:0] out_2
);

  wire and_1_out, button_1_out, clock_1_out;
  wire [7:0] adder_1_out, register_1_q;

  Register register_1 (.D(adder_1_out), .en(1'b1), .clk(clock_1_out), .Q(register_1_q), .clr(button_1_out));
  Adder adder_1 (.a(register_1_q), .b(8'h1), .out(adder_1_out), .cin(1'b0));  // open: cout
  Clock #(.highDuration(2), .lowDuration(2)) clock_1 (.out(clock_1_out));
  Button button_1 (.out(button_1_out));
  and and_1 (and_1_out, out_1[0], out_1[1]);
  dual_port_ram dual_port_ram_1 (
    .addr({8{1'b1}}), .pc(register_1_q), .d(register_1_q), .w(and_1_out), .instr(out_1), .data(out_2));
endmodule

module dual_port_ram (
  input  [7:0] addr,
  input  [7:0] pc,
  input  [7:0] d,
  input  w,
  output [7:0] instr,
  output [7:0] data
);

  wire clock_1_out, or_1_out;
  wire [7:0] multiplexer_1_out;

  Clock #(.highDuration(2), .lowDuration(2)) clock_1 (.out(clock_1_out));
  // Probe on multiplexer_1_out
  or or_1 (or_1_out, w, clock_1_out);
  Multiplexer #(.width(8)) multiplexer_1 (.in0(addr), .in1(pc), .out(multiplexer_1_out), .sel(clock_1_out));
  RAM #(.asyncread("true")) ram_1 (
    .addr(multiplexer_1_out), .we(or_1_out), .oe(1'b1), .clk(clock_1_out), .din(d), .dout(data));
  Register #(.trigger("falling")) pcbuf (.D(data), .en(1'b1), .clk(clock_1_out), .Q(instr));  // open: clr
endmodule

module ULA (
  input  [7:0] A,
  input  [7:0] B,
  input  [3:0] op_ula,
  output [7:0] Data
);

  wire comparator_1_eq;
  wire [2:0] bit_extender_1_out, bit_extender_2_out;
  wire [7:0] adder_1_out, adder_2_out, and_1_out, bit_extender_3_out, multiplier_1_out, negator_1_out,
       or_1_out, shifter_1_out, shifter_2_out, subtractor_1_out, xor_1_out;

  Bit_Extender #(.out_width(3)) bit_extender_1 (.in(B), .out(bit_extender_1_out));
  Bit_Extender #(.out_width(3)) bit_extender_2 (.in(B), .out(bit_extender_2_out));
  Comparator comparator_1 (.a({8{1'b0}}), .b(A), .eq(comparator_1_eq));  // open: gt, lt
  Negator negator_1 (.in(B), .out(negator_1_out));
  assign and_1_out = A & B;  // AND_Gate and_1, 8 bits wide
  assign or_1_out = A | B;  // OR_Gate or_1, 8 bits wide
  assign xor_1_out = A ^ B;  // XOR_Gate xor_1, 8 bits wide
  Adder adder_1 (.a(A), .b(B), .out(adder_1_out));  // open: cin, cout
  Subtractor subtractor_1 (.a(A), .b(B), .out(subtractor_1_out));  // open: bin, bout
  Shifter shifter_1 (.in(A), .\dist (bit_extender_1_out), .out(shifter_1_out));
  Shifter #(.shift("lr")) shifter_2 (.in(A), .\dist (bit_extender_2_out), .out(shifter_2_out));
  Multiplier multiplier_1 (.a(A), .b(B), .out(multiplier_1_out));  // open: cin, cout
  Adder adder_2 (.a(A), .b(8'h1), .out(adder_2_out));  // open: cin, cout
  assign bit_extender_3_out = {{7{1'b0}}, comparator_1_eq};  // Bit_Extender bit_extender_3
  Multiplexer #(.select(4), .width(8)) multiplexer_1 (
    .in0(bit_extender_3_out), .in1(negator_1_out), .in2(and_1_out), .in3(or_1_out), .in4(xor_1_out),
    .in5(adder_1_out), .in6(subtractor_1_out), .in7(shifter_1_out), .in8(shifter_2_out),
    .in9(multiplier_1_out), .in10(adder_2_out), .out(Data), .sel(op_ula));  // open: in11, in12, in13, in14, in15
endmodule

module Banco_Reg (
  input  Write,
  input  [1:0] Ra,
  input  [7:0] Data,
  input  [1:0] Rb,
  input  Reset_Breg,
  output [7:0] Saida_A,
  output [7:0] Saida_B
);

  wire clock_1_out, demultiplexer_1_out0, demultiplexer_1_out1, demultiplexer_1_out2, demultiplexer_1_out3;
  wire [7:0] multiplexer_1_out, multiplexer_2_out, multiplexer_3_out, multiplexer_4_out, x0, x1, x2, x3;

  Demultiplexer #(.select(2)) demultiplexer_1 (
    .out0(demultiplexer_1_out0), .out1(demultiplexer_1_out1), .out2(demultiplexer_1_out2),
    .out3(demultiplexer_1_out3), .in(Write), .sel(Ra));
  Clock #(.highDuration(2), .lowDuration(2)) clock_1 (.out(clock_1_out));
  Multiplexer #(.width(8)) multiplexer_1 (.in0(x0), .in1(Data), .out(multiplexer_1_out), .sel(demultiplexer_1_out0));
  Multiplexer #(.width(8)) multiplexer_2 (.in0(x1), .in1(Data), .out(multiplexer_2_out), .sel(demultiplexer_1_out1));
  Multiplexer #(.width(8)) multiplexer_3 (.in0(x2), .in1(Data), .out(multiplexer_3_out), .sel(demultiplexer_1_out2));
  Multiplexer #(.width(8)) multiplexer_4 (.in0(x3), .in1(Data), .out(multiplexer_4_out), .sel(demultiplexer_1_out3));
  Register u_x0 (.D(multiplexer_1_out), .clk(clock_1_out), .Q(x0), .clr(Reset_Breg));  // open: en
  Register u_x1 (.D(multiplexer_2_out), .clk(clock_1_out), .Q(x1), .clr(Reset_Breg));  // open: en
  Register u_x2 (.D(multiplexer_3_out), .clk(clock_1_out), .Q(x2), .clr(Reset_Breg));  // open: en
  Register u_x3 (.D(multiplexer_4_out), .clk(clock_1_out), .Q(x3), .clr(Reset_Breg));  // open: en
  Multiplexer #(.select(2), .width(8)) multiplexer_5 (.in0(x0), .in1(x1), .in2(x2), .in3(x3), .out(Saida_A), .sel(Ra));
  Multiplexer #(.select(2), .width(8)) multiplexer_6 (.in0(x0), .in1(x1), .in2(x2), .in3(x3), .out(Saida_B), .sel(Rb));
endmodule

module Unidade_Controle (
  input  [3:0] opcode,
  output [3:0] op_ula,
  output write_Breg,
  output write_mem,
  output mux_PCIMM,
  output mux_IMM,
  output mux_PCRb,
  output [1:0] mux_Data,
  output mux_JR
);

  wire and_1_out, and_2_out, and_3_out, and_4_out, and_5_out, and_6_out, and_7_out, and_8_out, and_9_out,
       and_10_out, and_11_out, and_12_out, and_13_out, and_14_out, and_15_out, and_18_out, and_19_out,
       and_20_out, and_21_out, not_1_out, not_2_out, not_3_out, not_4_out;

  not not_1 (not_1_out, opcode[3]);
  not not_2 (not_2_out, opcode[2]);
  not not_3 (not_3_out, opcode[1]);
  not not_4 (not_4_out, opcode[0]);
  and and_1 (and_1_out, not_1_out, opcode[2], opcode[0]);
  and and_2 (and_2_out, not_1_out, opcode[2], opcode[1]);
  and and_3 (and_3_out, opcode[2], opcode[1], opcode[0]);
  and and_4 (and_4_out, not_2_out, opcode[1], opcode[0]);
  and and_5 (and_5_out, opcode[2], not_3_out, not_4_out);
  and and_6 (and_6_out, opcode[3], opcode[2], not_3_out);
  and and_7 (and_7_out, opcode[3], opcode[2], not_4_out);
  and and_8 (and_8_out, not_3_out, opcode[0]);
  and and_9 (and_9_out, not_2_out, opcode[1], not_4_out);
  and and_10 (and_10_out, opcode[3], opcode[1], not_4_out);
  and and_11 (and_11_out, opcode[2], not_4_out);
  and and_12 (and_12_out, not_1_out, opcode[2], opcode[1]);
  and and_13 (and_13_out, opcode[3], not_4_out);
  and and_14 (and_14_out, opcode[1], not_4_out);
  and and_15 (and_15_out, opcode[2], not_3_out);
  and and_16 (write_mem, not_1_out, not_2_out, opcode[1], opcode[0]);
  and and_17 (mux_PCIMM, not_1_out, not_2_out, not_3_out, opcode[0]);
  and and_18 (and_18_out, not_1_out, not_2_out, not_3_out, opcode[0]);
  and and_19 (and_19_out, not_1_out, opcode[2], not_3_out, not_4_out);
  and and_20 (and_20_out, not_1_out, not_2_out, not_3_out, not_4_out);
  and and_21 (and_21_out, not_1_out, opcode[2], opcode[1], opcode[0]);
  and and_22 (mux_Data[1], not_1_out, not_2_out, opcode[1], not_4_out);
  and and_23 (mux_Data[0], not_1_out, not_2_out, opcode[1], opcode[0]);
  and and_24 (mux_JR, not_1_out, opcode[2], opcode[1], opcode[0]);
  or or_1 (op_ula[3], and_1_out, and_2_out, and_3_out);
  or or_2 (op_ula[2], and_4_out, and_5_out, and_6_out, and_7_out);
  or or_3 (op_ula[1], and_8_out, and_9_out, and_10_out);
  or or_4 (op_ula[0], and_11_out, and_12_out, and_13_out);
  or or_5 (write_Breg, and_14_out, and_15_out, opcode[3]);
  or or_6 (mux_IMM, and_18_out, and_19_out);
  or or_7 (mux_PCRb, and_20_out, and_21_out);
endmodule
