// Logisim project trabalho3_arq.circ as structural Verilog: 9 circuits, main circuit main
module main (
);

  wire clock_1_out, comparator_1_eq, L1_MOVE_SIGN, mux_mov, RESET, w_brg_L1, w_brg_L3, w_brg_L4, w_ram;
  wire [1:0] pc_sign, RA_L2, RA_L3, RA_L4, RB_L2, RB_L3, RB_L4;
  wire [3:0] IMM_L1, pc_1_inst, pc_1_inst_2, pc_1_inst_4;
  wire [7:0] A_L1, A_L2, A_L3, A_L4, addr, B_L1, B_L2, B_L3, B_L4, data_L1, data_L3, data_L4, data_ram,
       multiplexer_1_out, pc_1_data, pc_1_pc_atual, pc_imm, r0;
  wire [23:20] pc_1_inst_3;

  Button u_RESET (.out(RESET));
  Clock clock_1 (.out(clock_1_out));
  LED led_1 (.in(clock_1_out));
  PC pc_1 (
    .ADDR_BREG(B_L2), .PC_IMM(pc_imm), .PC_SIGN(pc_sign), .reset(RESET), .ADDR_L1(addr), .W_RAM(w_ram),
    .RAM_DATA_L1(data_L1), .pc_atual(pc_1_pc_atual),
    .Inst({pc_1_inst_4, IMM_L1, pc_1_inst_3, RA_L2, RB_L2, pc_1_inst_2, RA_L3, RB_L3, pc_1_inst, RA_L4, RB_L4}),
    .DATA(pc_1_data));
  // Probe on {pc_1_inst_4, IMM_L1, pc_1_inst_3, RA_L2, RB_L2, pc_1_inst_2, RA_L3, RB_L3, pc_1_inst, RA_L4, RB_L4}
  Comparator #(.width(4)) comparator_1 (.a(pc_1_inst_4), .b(4'b0100), .eq(comparator_1_eq));  // open: gt, lt
  Lane_3_4 lane_3_4_1 (.B(B_L4), .A(A_L4), .OPCODE(pc_1_inst), .Data(data_L4), .write_breg(w_brg_L4));
  Lane_3_4 lane_3_4_2 (.B(B_L3), .A(A_L3), .OPCODE(pc_1_inst_2), .Data(data_L3), .write_breg(w_brg_L3));
  Lane_2 lane_2_1 (
    .INST({pc_1_inst_3, RA_L2, RB_L2}), .A(A_L2), .B(B_L2), .PC(pc_1_pc_atual), .X0(r0), .pc_sign(pc_sign),
    .next_pc(pc_imm));
  Lane_1 lane_1_1 (
    .INST({pc_1_inst_4, IMM_L1}), .A(A_L1), .B(B_L1), .DATA_RAM(pc_1_data), .data_ram_out(data_L1),
    .addr(addr), .data_breg(data_ram), .w_breg_L1(w_brg_L1), .w_ram(w_ram), .L1_mov_sign(L1_MOVE_SIGN),
    .MUX_MOV(mux_mov));
  Multiplexer #(.width(8)) multiplexer_1 (
    .in0(data_L1), .in1(data_ram), .out(multiplexer_1_out), .sel(comparator_1_eq));
  B_Reg b_reg_1 (
    .RA_L1(IMM_L1[3:2]), .RA_L2(RA_L2), .RA_L3(RA_L3), .RA_L4(RA_L4), .RB_L1(IMM_L1[1:0]), .RB_L2(RB_L2),
    .RB_L3(RB_L3), .RB_L4(RB_L4), .DATA_L1(multiplexer_1_out), .DATA_L3(data_L3), .DATA_L4(data_L4),
    .W_BREG_L1(w_brg_L1), .W_BREG_L3(w_brg_L3), .W_BREG_L4(w_brg_L4), .L1_MOV_SIGN(L1_MOVE_SIGN),
    .MUX_MOV(mux_mov), .IMM_L1(IMM_L1), .reset(RESET), .Saida_A_L1(A_L1), .Saida_B_L1(B_L1),
    .Saida_A_L2(A_L2), .Saida_B_L2(B_L2), .Saida_A_L3(A_L3), .Saida_B_L3(B_L3), .Saida_A_L4(A_L4),
    .Saida_B_L4(B_L4), .R0(r0));

  // Other names for the same wires on the sheet: RB_L1[1:0] = IMM_L1[1:0]; RA_L1[1:0] = IMM_L1[3:2]

  // Notes on the sheet:
  //   Caso seja um load,
  //   manda o dado que vem da memoria para o breg
endmodule

module PC (
  input  [7:0] ADDR_BREG,
  input  [7:0] PC_IMM,
  input  [1:0] PC_SIGN,
  input  reset,
  input  [7:0] ADDR_L1,
  input  W_RAM,
  input  [7:0] RAM_DATA_L1,
  output [7:0] pc_atual,
  output [31:0] Inst,
  output [7:0] DATA
);

  wire clock_1_out, dualram_1_p2, dualram_1_p4, dualram_1_p10;
  wire [7:0] multiplexer_1_out, PC_1;
  wire [31:0] bit_extender_1_out;
  wire [31:8] dualram_1_p12;

  Multiplexer #(.select(2), .width(8)) multiplexer_1 (
    .in0(PC_1), .in1(ADDR_BREG), .in2(PC_IMM), .out(multiplexer_1_out), .sel(PC_SIGN));  // open: in3
  Register register_1 (.D(multiplexer_1_out), .en(1'b1), .clk(clock_1_out), .Q(pc_atual), .clr(reset));
  Clock clock_1 (.out(clock_1_out));
  Adder adder_1 (.a(pc_atual), .b(8'h1), .out(PC_1));  // open: cin, cout
  assign bit_extender_1_out = {{24{1'b0}}, RAM_DATA_L1};  // Bit_Extender bit_extender_1
  // DualRAM #(.asyncread("true"), .clearpin("true"), .dataWidth(32)) dualram_1: pin names not known; wires that end beside it: pc_atual, dualram_1_p2, 1'b1, dualram_1_p4, ADDR_L1, W_RAM, 1'b1, dualram_1_p4, bit_extender_1_out, dualram_1_p10, Inst, {dualram_1_p12, DATA}
  not not_1 (dualram_1_p2, 1'b1);
  Clock clock_2 (.out(dualram_1_p4));
  Button button_1 (.out(dualram_1_p10));
endmodule

module B_Reg (
  input  [1:0] RA_L1,
  input  [1:0] RA_L2,
  input  [1:0] RA_L3,
  input  [1:0] RA_L4,
  input  [1:0] RB_L1,
  input  [1:0] RB_L2,
  input  [1:0] RB_L3,
  input  [1:0] RB_L4,
  input  [7:0] DATA_L1,
  input  [7:0] DATA_L3,
  input  [7:0] DATA_L4,
  input  W_BREG_L1,
  input  W_BREG_L3,
  input  W_BREG_L4,
  input  L1_MOV_SIGN,
  input  MUX_MOV,
  input  [3:0] IMM_L1,
  input  reset,
  output [7:0] Saida_A_L1,
  output [7:0] Saida_B_L1,
  output [7:0] Saida_A_L2,
  output [7:0] Saida_B_L2,
  output [7:0] Saida_A_L3,
  output [7:0] Saida_B_L3,
  output [7:0] Saida_A_L4,
  output [7:0] Saida_B_L4,
  output [7:0] R0
);

  wire and_1_out, and_2_out, and_3_out, and_4_out, and_5_out, and_6_out, and_7_out, and_8_out, and_9_out,
       and_10_out, and_11_out, and_12_out, clock_1_out, clock_2_out, clock_3_out, clock_4_out,
       comparator_1_eq, comparator_2_eq, comparator_3_eq, comparator_4_eq, comparator_5_eq, comparator_6_eq,
       comparator_7_eq, comparator_8_eq, comparator_9_eq, comparator_10_eq, comparator_11_eq,
       comparator_12_eq, or_3_out, or_4_out, or_5_out, or_6_out, or_9_out, or_10_out;
  wire [1:0] bit0_out, bit_0_out, or_2_out, or_8_out;
  wire [7:0] MOV_DATA, multiplexer_1_out, multiplexer_2_out, multiplexer_3_out, multiplexer_5_out,
       multiplexer_6_out, x1, x2, x3;

  Comparator #(.width(2)) comparator_1 (.a(RA_L1), .b(2'b00), .eq(comparator_1_eq));  // open: gt, lt
  Comparator #(.width(2)) comparator_2 (.a(RA_L1), .b(2'b10), .eq(comparator_2_eq));  // open: gt, lt
  Comparator #(.width(2)) comparator_3 (.a(RA_L3), .b(2'b10), .eq(comparator_3_eq));  // open: gt, lt
  Comparator #(.width(2)) comparator_4 (.a(RA_L4), .b(2'b10), .eq(comparator_4_eq));  // open: gt, lt
  and and_1 (and_1_out, comparator_1_eq, W_BREG_L1);
  Comparator #(.width(2)) comparator_5 (.a(RA_L3), .b(2'b00), .eq(comparator_5_eq));  // open: gt, lt
  Comparator #(.width(2)) comparator_6 (.a(RA_L4), .b(2'b00), .eq(comparator_6_eq));  // open: gt, lt
  or or_1 (or_2_out[1], comparator_3_eq, comparator_4_eq);
  or or_2 (or_2_out[0], comparator_4_eq, comparator_2_eq);
  Multiplexer #(.width(8)) multiplexer_1 (.in0(DATA_L1), .in1(MOV_DATA), .out(multiplexer_1_out), .sel(L1_MOV_SIGN));
  or or_3 (or_3_out, L1_MOV_SIGN, and_1_out);
  and and_2 (and_2_out, comparator_5_eq, W_BREG_L3);
  and and_3 (and_3_out, comparator_6_eq, W_BREG_L4);
  Clock clock_1 (.out(clock_1_out));
  or or_4 (or_4_out, or_3_out, and_2_out, and_3_out);
  or or_5 (or_5_out, or_3_out, comparator_1_eq);
  or bit0 (bit0_out[0], or_5_out, comparator_6_eq);
  or bit1 (bit0_out[1], comparator_6_eq, comparator_5_eq);
  Multiplexer #(.select(2), .width(8)) multiplexer_2 (
    .in1(DATA_L1), .in2(DATA_L3), .in3(DATA_L4), .out(multiplexer_2_out));  // open: in0, sel
  Clock clock_2 (.out(clock_2_out));
  and and_4 (and_4_out, comparator_2_eq, W_BREG_L1, ~L1_MOV_SIGN);  // AND_Gate
  and and_5 (and_5_out, comparator_3_eq, W_BREG_L3);
  and and_6 (and_6_out, comparator_4_eq, W_BREG_L4);
  // Probe on multiplexer_1_out
  Register register_1 (.D(multiplexer_3_out), .en(or_4_out), .clk(clock_1_out), .Q(R0), .clr(reset));
  Multiplexer #(.select(2), .width(8)) multiplexer_3 (
    .in1(multiplexer_1_out), .in2(DATA_L3), .in3(DATA_L4), .out(multiplexer_3_out), .sel(bit0_out));  // open: in0
  Register register_2 (.D(multiplexer_2_out), .en(or_6_out), .clk(clock_2_out), .Q(x2), .clr(reset));
  or or_6 (or_6_out, and_4_out, and_5_out, and_6_out);
  Comparator #(.width(2)) comparator_7 (.a(RA_L1), .b(2'b11), .eq(comparator_7_eq));  // open: gt, lt
  Comparator #(.width(2)) comparator_8 (.a(RA_L3), .b(2'b11), .eq(comparator_8_eq));  // open: gt, lt
  Comparator #(.width(2)) comparator_9 (.a(RA_L4), .b(2'b11), .eq(comparator_9_eq));  // open: gt, lt
  Comparator #(.width(2)) comparator_10 (.a(RA_L1), .b(2'b01), .eq(comparator_10_eq));  // open: gt, lt
  Comparator #(.width(2)) comparator_11 (.a(RA_L3), .b(2'b01), .eq(comparator_11_eq));  // open: gt, lt
  Comparator #(.width(2)) comparator_12 (.a(RA_L4), .b(2'b01), .eq(comparator_12_eq));  // open: gt, lt
  or or_7 (or_8_out[1], comparator_8_eq, comparator_9_eq);
  Multiplexer #(.width(8)) multiplexer_4 (
    .in0({IMM_L1, R0[3:0]}), .in1({R0[7:4], IMM_L1}), .out(MOV_DATA), .sel(MUX_MOV));
  or bit_1 (bit_0_out[1], comparator_11_eq, comparator_12_eq);
  or or_8 (or_8_out[0], comparator_9_eq, comparator_7_eq);
  or bit_0 (bit_0_out[0], comparator_12_eq, comparator_10_eq);
  and and_7 (and_7_out, comparator_7_eq, W_BREG_L1, ~L1_MOV_SIGN);  // AND_Gate
  and and_8 (and_8_out, comparator_8_eq, W_BREG_L3);
  and and_9 (and_9_out, comparator_9_eq, W_BREG_L4);
  // Probe on {R0[7:4], IMM_L1}
  and and_10 (and_10_out, comparator_10_eq, W_BREG_L1, ~L1_MOV_SIGN);  // AND_Gate
  and and_11 (and_11_out, comparator_11_eq, W_BREG_L3);
  and and_12 (and_12_out, comparator_12_eq, W_BREG_L4);
  Multiplexer #(.select(2), .width(8)) multiplexer_5 (
    .in1(DATA_L1), .in2(DATA_L3), .in3(DATA_L4), .out(multiplexer_5_out));  // open: in0, sel
  Register register_3 (.D(multiplexer_5_out), .en(or_9_out), .clk(clock_3_out), .Q(x3), .clr(reset));
  Clock clock_3 (.out(clock_3_out));
  or or_9 (or_9_out, and_7_out, and_8_out, and_9_out);
  Multiplexer #(.select(2), .width(8)) multiplexer_6 (
    .in1(DATA_L1), .in2(DATA_L3), .in3(DATA_L4), .out(multiplexer_6_out));  // open: in0, sel
  Register register_4 (.D(multiplexer_6_out), .en(or_10_out), .clk(clock_4_out), .Q(x1), .clr(reset));
  Clock clock_4 (.out(clock_4_out));
  or or_10 (or_10_out, and_10_out, and_11_out, and_12_out);
  Multiplexer #(.select(2), .width(8)) multiplexer_7 (
    .in0(R0), .in1(x1), .in2(x2), .in3(x3), .out(Saida_A_L1), .sel(RA_L1));
  Multiplexer #(.select(2), .width(8)) multiplexer_8 (
    .in0(R0), .in1(x1), .in2(x2), .in3(x3), .out(Saida_A_L2), .sel(RA_L2));
  Multiplexer #(.select(2), .width(8)) multiplexer_9 (
    .in0(R0), .in1(x1), .in2(x2), .in3(x3), .out(Saida_A_L3), .sel(RA_L3));
  Multiplexer #(.select(2), .width(8)) multiplexer_10 (
    .in0(R0), .in1(x1), .in2(x2), .in3(x3), .out(Saida_A_L4), .sel(RA_L4));
  Multiplexer #(.select(2), .width(8)) multiplexer_11 (
    .in0(R0), .in1(x1), .in2(x2), .in3(x3), .out(Saida_B_L1), .sel(RB_L1));
  Multiplexer #(.select(2), .width(8)) multiplexer_12 (
    .in0(R0), .in1(x1), .in2(x2), .in3(x3), .out(Saida_B_L2), .sel(RB_L2));
  Multiplexer #(.select(2), .width(8)) multiplexer_13 (
    .in0(R0), .in1(x1), .in2(x2), .in3(x3), .out(Saida_B_L3), .sel(RB_L3));
  Multiplexer #(.select(2), .width(8)) multiplexer_14 (
    .in0(R0), .in1(x1), .in2(x2), .in3(x3), .out(Saida_B_L4), .sel(RB_L4));

  // Other names for the same wires on the sheet: MOVH_OUT[7:0] = {IMM_L1, R0[3:0]}; MOVL_OUT[7:0] = {R0[7:4], IMM_L1};
  //   x0[7:0] = R0
endmodule

module Lane_1 (
  input  [7:0] INST,
  input  [7:0] A,
  input  [7:0] B,
  input  [7:0] DATA_RAM,
  output [7:0] data_ram_out,
  output [7:0] addr,
  output [7:0] data_breg,
  output w_breg_L1,
  output w_ram,
  output L1_mov_sign,
  output MUX_MOV
);

  wire ld, movh, movl;

  and and_1 (ld, ~INST[4], ~INST[5], INST[6], ~INST[7]);  // AND_Gate
  and and_2 (w_ram, INST[4], ~INST[5], INST[6], ~INST[7]);  // AND_Gate
  and and_3 (movh, ~INST[4], INST[5], INST[6], ~INST[7]);  // AND_Gate
  and and_4 (movl, INST[4], INST[5], INST[6], ~INST[7]);  // AND_Gate
  or or_1 (L1_mov_sign, movh, movl);
  or or_2 (w_breg_L1, ld, w_ram, movl);

  assign addr = B;
  assign data_breg = DATA_RAM;
  assign data_ram_out = A;
  assign MUX_MOV = INST[4];

  // Other names for the same wires on the sheet: opcode[3:0] = INST[7:4]; st = w_ram
endmodule

module Lane_2 (
  input  [7:0] INST,
  input  [7:0] A,
  input  [7:0] B,
  input  [7:0] PC,
  input  [7:0] X0,
  output [1:0] pc_sign,
  output [7:0] next_pc
);

  wire and_5_out, and_6_out, brzi, brzr, comparator_1_eq, comparator_2_eq, j_imm, jr;
  wire [3:0] not_1_out;
  wire [7:0] bit_extender_1_out;

  assign not_1_out = ~INST[7:4];  // NOT_Gate not_1, 4 bits wide
  and and_1 (brzr, not_1_out[0], not_1_out[1], not_1_out[2], not_1_out[3]);
  and and_2 (brzi, ~not_1_out[0], not_1_out[1], not_1_out[2], not_1_out[3]);  // AND_Gate
  and and_3 (jr, not_1_out[0], ~not_1_out[1], not_1_out[2], not_1_out[3]);  // AND_Gate
  and and_4 (j_imm, ~not_1_out[0], ~not_1_out[1], not_1_out[2], not_1_out[3]);  // AND_Gate
  Comparator comparator_1 (.a(A), .b({8{1'b0}}), .eq(comparator_1_eq));  // open: gt, lt
  Comparator comparator_2 (.a({8{1'b0}}), .b(X0), .eq(comparator_2_eq));  // open: gt, lt
  and and_5 (and_5_out, brzr, comparator_1_eq);
  and and_6 (and_6_out, comparator_2_eq, brzi);
  assign bit_extender_1_out = {{4{INST[3]}}, INST[3:0]};  // Bit_Extender bit_extender_1
  or or_1 (pc_sign[0], and_5_out, jr);
  or or_2 (pc_sign[1], and_6_out, j_imm);
  Adder adder_1 (.a(bit_extender_1_out), .b(PC), .out(next_pc));  // open: cin, cout

  // Other names for the same wires on the sheet: imm[3:0] = INST[3:0]; opcode[3:0] = INST[7:4];
  //   Salto_Reg = pc_sign[0]; Salto_IMM = pc_sign[1]; R0[7:0] = X0; RA[7:0] = A; RB[7:0] = B
endmodule

module Lane_3_4 (
  input  [7:0] B,
  input  [7:0] A,
  input  [3:0] OPCODE,
  output [7:0] Data,
  output write_breg
);

  wire [2:0] bit_extender_1_out;
  wire [7:0] adder_1_out, and_1_out, not_logical_1_out_2, or_1_out, shifter_1_out, shifter_2_out,
       subtractor_1_out;

  Bit_Extender #(.out_width(3)) bit_extender_1 (.in(B), .out(bit_extender_1_out));
  Adder adder_1 (.a(A), .b(B), .out(adder_1_out));  // open: cin, cout
  Subtractor subtractor_1 (.a(A), .b(B), .out(subtractor_1_out));  // open: bin, bout
  assign and_1_out = A & B;  // AND_Gate and_1, 8 bits wide
  assign or_1_out = A | B;  // OR_Gate or_1, 8 bits wide
  Shifter shifter_1 (.in(A), .\dist (bit_extender_1_out), .out(shifter_1_out));
  Shifter #(.shift("lr")) shifter_2 (.in(A), .\dist (bit_extender_1_out), .out(shifter_2_out));
  not_logical not_logical_1 (.B(B), .out_2(not_logical_1_out_2));
  Multiplexer #(.select(4), .width(8)) multiplexer_1 (
    .in8(adder_1_out), .in9(subtractor_1_out), .in10(and_1_out), .in11(or_1_out), .in12(not_logical_1_out_2),
    .in13(shifter_1_out), .in14(shifter_2_out), .out(Data), .sel(OPCODE));  // open: in0, in1, in2, in3, in4, in5, in6, in7, in15
  nand nand_1 (write_breg, OPCODE[0], OPCODE[1], OPCODE[2], OPCODE[3]);
endmodule

module Decodificador_1 (
  input  [7:0] inst,
  output [1:0] Rb,
  output [1:0] Ra,
  output [3:0] Opcode
);


  assign Opcode = inst[7:4];
  assign Ra = inst[3:2];
  assign Rb = inst[1:0];
endmodule

module Decodificador_2 (
  input  [7:0] inst,
  output [3:0] Imm,
  output [3:0] Opcode
);


  assign Imm = inst[3:0];
  assign Opcode = inst[7:4];
endmodule

module not_logical (
  input  [7:0] B,
  output [7:0] out_2
);

  wire comparator_1_gt, comparator_1_lt, nor_1_out;

  Comparator comparator_1 (.a(B), .b({8{1'b0}}), .gt(comparator_1_gt), .lt(comparator_1_lt));  // open: eq
  nor nor_1 (nor_1_out, comparator_1_gt, comparator_1_lt);
  assign out_2 = {{7{1'b0}}, nor_1_out};  // Bit_Extender bit_extender_1
endmodule
