// Logisim project semaforo.circ as structural Verilog: 1 circuit, main circuit main
module main (
);

  wire and_1_out, and_2_out, and_3_out, and_4_out, and_5_out, clock_1_out, d_ff_1_q, d_ff_1_qn, d_ff_2_q,
       d_ff_2_qn;

  Clock clock_1 (.out(clock_1_out));
  and and_1 (and_1_out, d_ff_1_qn, d_ff_2_qn);
  and and_2 (and_2_out, d_ff_2_qn, d_ff_1_q);
  D_Flip_Flop d_ff_1 (.clk(clock_1_out), .D(and_1_out), .Q(d_ff_1_q), .Qn(d_ff_1_qn));  // open: preset, en, reset
  D_Flip_Flop d_ff_2 (.clk(clock_1_out), .D(and_2_out), .Q(d_ff_2_q), .Qn(d_ff_2_qn));  // open: preset, en, reset
  and and_3 (and_3_out, d_ff_2_qn, d_ff_1_qn);
  and and_4 (and_4_out, d_ff_1_q, d_ff_2_qn);
  and and_5 (and_5_out, d_ff_2_q, d_ff_1_qn);
  LED led_1 (.in(and_3_out));
  LED led_2 (.in(and_5_out));
  LED led_3 (.in(and_4_out));
endmodule
