// Logisim project sequencia123.circ as structural Verilog: 2 circuits, main circuit main
module main (
);

  wire _1_out, _2_out, _3_out, and_1_out, and_2_out, and_3_out, and_4_out, and_5_out, and_6_out, and_7_out,
       and_8_out, and_9_out, and_10_out, and_11_out, and_12_out, and_13_out, and_14_out, and_15_out,
       and_16_out, and_17_out, and_18_out, and_19_out, en, i0, I0_out, i1, I1_out, not_1_out, not_2_out,
       not_3_out, not_4_out, not_5_out, not_6_out, not_7_out, or_2_out, or_3_out, or_4_out, or_5_out,
       or_6_out, or_7_out, s0, s0_t, s1, s1_t, s2, s2_t;

  Button _1 (.out(_1_out));
  Button _2 (.out(_2_out));
  Button _3 (.out(_3_out));
  or or_1 (en, _3_out, _2_out, _1_out);
  not not_1 (not_1_out, _1_out);
  not not_2 (not_2_out, _2_out);
  or u_I0 (I0_out, not_1_out, _2_out, _3_out);
  or u_I1 (I1_out, _3_out, not_2_out, _1_out);
  or or_2 (or_2_out, _3_out, _2_out, _1_out);
  and i0_2 (i0, or_2_out, I0_out);
  and i1_2 (i1, I1_out, or_2_out);
  and and_1 (and_1_out, i0, i1, s0, s1_t);
  and and_2 (and_2_out, i0, s0, s1_t, s2);
  not not_3 (not_3_out, i1);
  and and_3 (and_3_out, i0, not_3_out, s1_t, s2);
  and and_4 (and_4_out, i1, s0, s1_t, s2);
  and and_5 (and_5_out, i0, i1, s0_t);
  and and_6 (and_6_out, i0, s0_t, s2_t);
  and and_7 (and_7_out, i0, not_3_out, s1_t, s0_t);
  and and_8 (and_8_out, i0, not_3_out, s0_t, s1);
  and and_9 (and_9_out, i1, s0_t);
  and and_10 (and_10_out, i0, i1, s1_t);
  and and_11 (and_11_out, i1, s1_t, s2);
  and and_12 (and_12_out, i0, s0, s1_t, s2);
  not not_4 (not_4_out, i0);
  not not_5 (not_5_out, i1);
  and and_13 (and_13_out, not_4_out, not_5_out, s0, s1_t, s2_t);
  or or_3 (or_3_out, and_1_out, and_2_out, and_3_out, and_4_out);
  or or_4 (or_4_out, and_5_out, and_6_out, and_7_out, and_8_out);
  or or_5 (or_5_out, and_9_out, and_10_out, and_11_out, and_12_out, and_13_out);
  flipflopd flipflopd_1 (.in_1(or_3_out), .out_3(s0), .out_4(s0_t), .in_2(en));
  flipflopd flipflopd_2 (.in_1(or_4_out), .out_3(s1), .out_4(s1_t), .in_2(en));
  flipflopd flipflopd_3 (.in_1(or_5_out), .out_3(s2), .out_4(s2_t), .in_2(en));
  not not_6 (not_6_out, i0);
  not not_7 (not_7_out, i1);
  and and_14 (and_14_out, not_6_out, not_7_out, not_7_out);
  and and_15 (and_15_out, i0, not_7_out);
  and and_16 (and_16_out, i0, i1);
  and and_17 (and_17_out, i0, i1, s2_t, s0, s1_t);
  and and_18 (and_18_out, s0, s1_t, s2);
  or or_6 (or_6_out, and_14_out, and_15_out, and_16_out);
  and and_19 (and_19_out, and_18_out, or_6_out);
  or or_7 (or_7_out, and_17_out, and_19_out);
  LED led_1 (.in(or_7_out));
endmodule

module flipflopd (
  input  in_1,
  input  in_2,
  output out_3,
  output out_4
);

  wire nand_1_out, nand_2_out, nand_3_out, nand_4_out, nand_5_out, nand_6_out, not_1_out, not_2_out;

  not not_1 (not_1_out, in_1);
  nand nand_1 (nand_1_out, in_1, in_2);
  nand nand_2 (nand_2_out, in_2, not_1_out);
  not not_2 (not_2_out, in_2);
  nand nand_3 (nand_3_out, nand_1_out, nand_4_out);
  nand nand_4 (nand_4_out, nand_3_out, nand_2_out);
  nand nand_5 (nand_5_out, nand_3_out, not_2_out);
  nand nand_6 (nand_6_out, not_2_out, nand_4_out);
  nand nand_7 (out_3, nand_5_out, out_4);
  nand nand_8 (out_4, out_3, nand_6_out);
endmodule
