// Logisim project trabalhoProjetos.circ as structural Verilog
module BancoDeRegistradores (
  input  [3:0] RS1,
  input  [3:0] RS2,
  input  [17:0] D,
  input  W,
  input  [3:0] RD,
  output [17:0] A,
  output [17:0] B
);

  wire clock_1_out, MUX_a0, MUX_a1, MUX_a2, MUX_s0, MUX_s1, MUX_s2, MUX_t0, MUX_t1, MUX_t2, MUX_t3, MUX_t4,
       MUX_t5, MUX_t6, MUX_x1, MUX_x2;
  wire [17:0] a0, a1, a2, multiplexer_1_out, multiplexer_2_out, multiplexer_3_out, multiplexer_4_out,
       multiplexer_5_out, multiplexer_6_out, multiplexer_7_out, multiplexer_8_out, multiplexer_9_out,
       multiplexer_10_out, multiplexer_11_out, multiplexer_12_out, multiplexer_13_out, multiplexer_14_out,
       multiplexer_15_out, s0, s1, s2, t0, t1, t2, t3, t4, t5, t6, undriven, x1, x2;

  Multiplexer #(.width(18)) multiplexer_1 (.in0(x1), .in1(D), .out(multiplexer_1_out), .sel(MUX_x1));
  Multiplexer #(.width(18)) multiplexer_2 (.in0(x2), .in1(D), .out(multiplexer_2_out), .sel(MUX_x2));
  Multiplexer #(.width(18)) multiplexer_3 (.in0(s0), .in1(D), .out(multiplexer_3_out), .sel(MUX_s0));
  Multiplexer #(.width(18)) multiplexer_4 (.in0(s1), .in1(D), .out(multiplexer_4_out), .sel(MUX_s1));
  Multiplexer #(.width(18)) multiplexer_5 (.in0(s2), .in1(D), .out(multiplexer_5_out), .sel(MUX_s2));
  Multiplexer #(.width(18)) multiplexer_6 (.in0(a0), .in1(D), .out(multiplexer_6_out), .sel(MUX_a0));
  Multiplexer #(.width(18)) multiplexer_7 (.in0(a1), .in1(D), .out(multiplexer_7_out), .sel(MUX_a1));
  Register #(.width(18)) u_x1 (.D(multiplexer_1_out), .clk(clock_1_out), .Q(x1));  // open: en, clr
  Register #(.width(18)) u_x2 (.D(multiplexer_2_out), .clk(clock_1_out), .Q(x2));  // open: en, clr
  Register #(.width(18)) u_s0 (.D(multiplexer_3_out), .clk(clock_1_out), .Q(s0));  // open: en, clr
  Register #(.width(18)) u_s1 (.D(multiplexer_4_out), .clk(clock_1_out), .Q(s1));  // open: en, clr
  Register #(.width(18)) u_s2 (.D(multiplexer_5_out), .clk(clock_1_out), .Q(s2));  // open: en, clr
  Register #(.width(18)) u_a0 (.D(multiplexer_6_out), .clk(clock_1_out), .Q(a0));  // open: en, clr
  Register #(.width(18)) u_a1 (.D(multiplexer_7_out), .clk(clock_1_out), .Q(a1));  // open: en, clr
  Clock clock_1 (.out(clock_1_out));
  Multiplexer #(.width(18)) multiplexer_8 (.in0(a2), .in1(undriven), .out(multiplexer_8_out), .sel(MUX_a2));
  Multiplexer #(.width(18)) multiplexer_9 (.in0(t0), .in1(undriven), .out(multiplexer_9_out), .sel(MUX_t0));
  Multiplexer #(.width(18)) multiplexer_10 (.in0(t1), .in1(undriven), .out(multiplexer_10_out), .sel(MUX_t1));
  Multiplexer #(.width(18)) multiplexer_11 (.in0(t2), .in1(undriven), .out(multiplexer_11_out), .sel(MUX_t2));
  Multiplexer #(.width(18)) multiplexer_12 (.in0(t3), .in1(undriven), .out(multiplexer_12_out), .sel(MUX_t3));
  Multiplexer #(.width(18)) multiplexer_13 (.in0(t4), .in1(undriven), .out(multiplexer_13_out), .sel(MUX_t4));
  Multiplexer #(.width(18)) multiplexer_14 (.in0(t5), .in1(undriven), .out(multiplexer_14_out), .sel(MUX_t5));
  Multiplexer #(.width(18)) multiplexer_15 (.in0(t6), .in1(undriven), .out(multiplexer_15_out), .sel(MUX_t6));
  Register #(.width(18)) u_a2 (.D(multiplexer_8_out), .clk(clock_1_out), .Q(a2));  // open: en, clr
  Register #(.width(18)) u_t0 (.D(multiplexer_9_out), .clk(clock_1_out), .Q(t0));  // open: en, clr
  Register #(.width(18)) u_t1 (.D(multiplexer_10_out), .clk(clock_1_out), .Q(t1));  // open: en, clr
  Register #(.width(18)) u_t2 (.D(multiplexer_11_out), .clk(clock_1_out), .Q(t2));  // open: en, clr
  Register #(.width(18)) u_t3 (.D(multiplexer_12_out), .clk(clock_1_out), .Q(t3));  // open: en, clr
  Register #(.width(18)) u_t4 (.D(multiplexer_13_out), .clk(clock_1_out), .Q(t4));  // open: en, clr
  Register #(.width(18)) u_t5 (.D(multiplexer_14_out), .clk(clock_1_out), .Q(t5));  // open: en, clr
  Register #(.width(18)) u_t6 (.D(multiplexer_15_out), .clk(clock_1_out), .Q(t6));  // open: en, clr
  Demultiplexer #(.select(4)) demultiplexer_1 (
    .out1(MUX_x1), .out2(MUX_x2), .out3(MUX_s0), .out4(MUX_s1), .out5(MUX_s2), .out6(MUX_a0), .out7(MUX_a1),
    .out8(MUX_a2), .out9(MUX_t0), .out10(MUX_t1), .out11(MUX_t2), .out12(MUX_t3), .out13(MUX_t4),
    .out14(MUX_t5), .out15(MUX_t6), .in(W), .sel(RD));  // open: out0
  Multiplexer #(.select(4), .width(18)) multiplexer_16 (
    .in0({18{1'b0}}), .in1(x1), .in2(x2), .in3(s0), .in4(s1), .in5(s2), .in6(a0), .in7(a1), .in8(a2),
    .in9(t0), .in10(t1), .in11(t2), .in12(t3), .in13(t4), .in14(t5), .in15(t6), .out(A), .sel(RS1));
  Multiplexer #(.select(4), .width(18)) multiplexer_17 (
    .in0({18{1'b0}}), .in1(x1), .in2(x2), .in3(s0), .in4(s1), .in5(s2), .in6(a0), .in7(a1), .in8(a2),
    .in9(t0), .in10(t1), .in11(t2), .in12(t3), .in13(t4), .in14(t5), .in15(t6), .out(B), .sel(RS2));
endmodule

module ULA (
);

  Comparator comparator_1 ();  // open: a, b, gt, eq, lt
  // AND_Gate and_1 is placed but not wired
  // OR_Gate or_1 is placed but not wired
  // XOR_Gate xor_1 is placed but not wired
  Adder adder_1 ();  // open: a, b, out, cin, cout
  Subtractor subtractor_1 ();  // open: a, b, out, bin, bout
  Shifter shifter_1 ();  // open: in, dist, out
  Shifter #(.shift("lr")) shifter_2 ();  // open: in, dist, out
  Multiplexer #(.select(4)) multiplexer_1 ();  // open: in0, in1, in2, in3, in4, in5, in6, in7, in8, in9, in10, in11, in12, in13, in14, in15, out, sel
endmodule
