// Logisim project Trabalho.circ as structural Verilog: 18 circuits, main circuit PLACAR MULTIESPORTIVO
module PLACAR_MULTIESPORTIVO (
);

  wire _1_out, _2_out, _3_out, _5_out, _7_out, main_1_led, main_1_out_7, main_1_out_8, main_1_out_9,
       main_1_out_10, main_1_out_11, main_1_out_12, main_1_out_13, main_1_out_14, main_1_out_15,
       main_1_out_16, main_1_out_17, main_1_out_18, main_1_out_19, main_1_out_20, undo_out;

  Button _1 (.out(_1_out));
  Button _2 (.out(_2_out));
  Button _5 (.out(_5_out));
  Button _3 (.out(_3_out));
  Button _7 (.out(_7_out));
  Button undo (.out(undo_out));
  main main_1 (
    .in_1(_1_out), .in_2(_2_out), .in_3(_3_out), .in_4(_5_out), .out_7(main_1_out_7), .out_8(main_1_out_8),
    .out_9(main_1_out_9), .out_10(main_1_out_10), .out_11(main_1_out_11), .out_12(main_1_out_12),
    .out_13(main_1_out_13), .out_14(main_1_out_14), .out_15(main_1_out_15), .out_16(main_1_out_16),
    .out_17(main_1_out_17), .out_18(main_1_out_18), .out_19(main_1_out_19), .out_20(main_1_out_20),
    .LED(main_1_led), .in_5(_7_out), .in_6(undo_out));
  _7_Segment_Display u_7_segment_display_1 (
    .g(main_1_out_17), .f(main_1_out_15), .a(main_1_out_14), .b(main_1_out_16), .e(main_1_out_18),
    .d(main_1_out_20), .c(main_1_out_19));  // open: dp
  _7_Segment_Display u_7_segment_display_2 (
    .g(main_1_out_10), .f(main_1_out_8), .a(main_1_out_7), .b(main_1_out_9), .e(main_1_out_11),
    .d(main_1_out_13), .c(main_1_out_12));  // open: dp
  LED led_1 (.in(main_1_led));
endmodule

module main (
  input  in_1,
  input  in_2,
  input  in_3,
  input  in_4,
  input  in_5,
  input  in_6,
  output out_7,
  output out_8,
  output out_9,
  output out_10,
  output out_11,
  output out_12,
  output out_13,
  output out_14,
  output out_15,
  output out_16,
  output out_17,
  output out_18,
  output out_19,
  output out_20,
  output LED
);

  wire Codificador_de_3_bits_out_6, Codificador_de_3_bits_out_7, Codificador_de_3_bits_out_8, enable_1_out_7,
       Memoria_Principal_out_8, Memoria_Principal_out_9, Memoria_Principal_out_10, Memoria_Principal_out_11,
       Memoria_Principal_out_12, Memoria_Principal_out_13, Memoria_Secundaria_out_5,
       Memoria_Secundaria_out_6, Memoria_Secundaria_out_7, ula_1_out_14, ula_1_out_15, ula_1_out_16,
       ula_1_out_17, ula_1_out_18, ula_1_out_19;

  Codificador Codificador_de_3_bits (
    .A(in_1), .B(in_2), .C(in_3), .D(in_4), .E(in_5), .out_6(Codificador_de_3_bits_out_6),
    .out_7(Codificador_de_3_bits_out_7), .out_8(Codificador_de_3_bits_out_8));
  memoria_2 Memoria_Secundaria (
    .out_5(Memoria_Secundaria_out_5), .in_2(Codificador_de_3_bits_out_6), .out_6(Memoria_Secundaria_out_6),
    .in_3(Codificador_de_3_bits_out_7), .out_7(Memoria_Secundaria_out_7), .in_4(Codificador_de_3_bits_out_8),
    .in_1(enable_1_out_7));
  ULA ula_1 (
    .B0(Codificador_de_3_bits_out_8), .M0(Memoria_Principal_out_8), .B1(Codificador_de_3_bits_out_7),
    .M1(Memoria_Principal_out_9), .B2(Codificador_de_3_bits_out_6), .M2(Memoria_Principal_out_10),
    .M3(Memoria_Principal_out_11), .M4(Memoria_Principal_out_12), .M5(Memoria_Principal_out_13),
    .out_14(ula_1_out_14), .out_15(ula_1_out_15), .out_16(ula_1_out_16), .out_17(ula_1_out_17),
    .out_18(ula_1_out_18), .out_19(ula_1_out_19), .in_13(in_6), .BM2(Memoria_Secundaria_out_5),
    .BM1(Memoria_Secundaria_out_6), .BM0(Memoria_Secundaria_out_7));
  enable enable_1 (
    .in_1(in_5), .in_2(in_4), .in_3(in_3), .in_4(in_2), .in_5(in_1), .out_7(enable_1_out_7), .in_6(in_6));
  memoria Memoria_Principal (
    .in_2(ula_1_out_14), .out_8(Memoria_Principal_out_8), .out_9(Memoria_Principal_out_9),
    .in_3(ula_1_out_15), .out_10(Memoria_Principal_out_10), .in_4(ula_1_out_16),
    .out_11(Memoria_Principal_out_11), .in_5(ula_1_out_17), .out_12(Memoria_Principal_out_12),
    .in_6(ula_1_out_18), .out_13(Memoria_Principal_out_13), .in_7(ula_1_out_19), .in_1(enable_1_out_7));
  Display_2 Dispaly_dezenas (
    .A(Memoria_Principal_out_13), .B(Memoria_Principal_out_12), .C(Memoria_Principal_out_11),
    .D(Memoria_Principal_out_10), .E(Memoria_Principal_out_9), .F(Memoria_Principal_out_8), .D8(out_7),
    .D9(out_8), .D10(out_9), .D11(out_10), .D12(out_11), .D13(out_12), .D14(out_13));
  Display_1 Display_unidades (
    .A(Memoria_Principal_out_13), .B(Memoria_Principal_out_12), .C(Memoria_Principal_out_11),
    .D(Memoria_Principal_out_10), .E(Memoria_Principal_out_9), .F(Memoria_Principal_out_8), .D1(out_14),
    .D2(out_15), .D3(out_16), .D4(out_17), .D5(out_18), .D6(out_19), .D7(out_20));
  luz_apito_final luz_apito_final_1 (
    .A(Memoria_Principal_out_13), .B(Memoria_Principal_out_12), .C(Memoria_Principal_out_11),
    .D(Memoria_Principal_out_10), .E(Memoria_Principal_out_9), .F(Memoria_Principal_out_8), .S(LED));

  // Other names for the same wires on the sheet: _1 = in_1; _2 = in_2; _3 = in_3; _5 = in_4; _7 = in_5; undo = in_6
endmodule

module Codificador (
  input  A,
  input  B,
  input  C,
  input  D,
  input  E,
  output out_6,
  output out_7,
  output out_8
);

  wire and_1_out, and_2_out, and_3_out, and_4_out, and_5_out, and_6_out, and_7_out, and_8_out, and_9_out,
       not_1_out, not_2_out, not_3_out, not_4_out, not_5_out;

  not not_1 (not_1_out, A);
  not not_2 (not_2_out, B);
  not not_3 (not_3_out, C);
  not not_4 (not_4_out, D);
  not not_5 (not_5_out, E);
  and and_1 (and_1_out, not_1_out, not_2_out, not_3_out, D, not_5_out);
  and and_2 (and_2_out, not_1_out, not_2_out, not_3_out, not_4_out, E);
  and and_3 (and_3_out, not_1_out, B, not_3_out, not_4_out, not_5_out);
  and and_4 (and_4_out, not_1_out, not_2_out, C, not_4_out, not_5_out);
  and and_5 (and_5_out, not_1_out, not_2_out, not_3_out, not_4_out, E);
  and and_6 (and_6_out, A, not_2_out, not_3_out, not_4_out, not_5_out);
  and and_7 (and_7_out, not_1_out, not_2_out, C, not_4_out, not_5_out);
  and and_8 (and_8_out, not_1_out, not_2_out, not_3_out, D, not_5_out);
  and and_9 (and_9_out, not_1_out, not_2_out, not_3_out, not_4_out, E);
  or or_1 (out_6, and_1_out, and_2_out);
  or or_2 (out_7, and_3_out, and_4_out, and_5_out);
  or or_3 (out_8, and_6_out, and_7_out, and_8_out, and_9_out);
endmodule

// ULA
module ULA (
  input  BM0,
  input  BM1,
  input  BM2,
  input  B0,
  input  B1,
  input  B2,
  input  M0,
  input  M1,
  input  M2,
  input  M3,
  input  M4,
  input  M5,
  input  in_13,
  output out_14,
  output out_15,
  output out_16,
  output out_17,
  output out_18,
  output out_19
);

  wire not_1_out, soma_out_10, soma_out_11, soma_out_12, soma_out_13, soma_out_14, soma_out_15, sub_out_10,
       sub_out_11, sub_out_12, sub_out_13, sub_out_14, sub_out_15;

  subtrador_da_ula sub (
    .B0(BM0), .M0(M0), .B1(BM1), .M1(M1), .B2(BM2), .M2(M2), .M3(M3), .M4(M4), .M5(M5), .out_10(sub_out_10),
    .out_11(sub_out_11), .out_12(sub_out_12), .out_13(sub_out_13), .out_14(sub_out_14), .out_15(sub_out_15));
  somador_da_ula soma (
    .B0(B0), .M0(M0), .B1(B1), .M1(M1), .B2(B2), .M2(M2), .M3(M3), .M4(M4), .M5(M5), .out_10(soma_out_10),
    .out_11(soma_out_11), .out_12(soma_out_12), .out_13(soma_out_13), .out_14(soma_out_14),
    .out_15(soma_out_15));
  Multiplexer multiplexer_1 (.in0(sub_out_10), .in1(soma_out_10), .out(out_14), .sel(not_1_out));  // open: en
  Multiplexer multiplexer_2 (.in0(sub_out_11), .in1(soma_out_11), .out(out_15), .sel(not_1_out));  // open: en
  Multiplexer multiplexer_3 (.in0(sub_out_12), .in1(soma_out_12), .out(out_16), .sel(not_1_out));  // open: en
  Multiplexer multiplexer_4 (.in0(sub_out_13), .in1(soma_out_13), .out(out_17), .sel(not_1_out));  // open: en
  Multiplexer multiplexer_5 (.in0(sub_out_14), .in1(soma_out_14), .out(out_18), .sel(not_1_out));  // open: en
  Multiplexer multiplexer_6 (.in0(sub_out_15), .in1(soma_out_15), .out(out_19), .sel(not_1_out));  // open: en
  not not_1 (not_1_out, in_13);
endmodule

module somador_completo (
  input  in_1,
  input  in_2,
  input  in_3,
  output out_4,
  output out_5
);

  wire and_1_out, and_2_out, and_3_out, xor_1_out;

  xor xor_1 (xor_1_out, in_1, in_2);
  and and_1 (and_1_out, in_2, in_3);
  and and_2 (and_2_out, in_3, in_1);
  and and_3 (and_3_out, in_1, in_2);
  xor xor_2 (out_4, xor_1_out, in_3);
  or or_1 (out_5, and_1_out, and_2_out, and_3_out);
endmodule

module Display_1 (
  input  A,
  input  B,
  input  C,
  input  D,
  input  E,
  input  F,
  output D1,
  output D2,
  output D3,
  output D4,
  output D5,
  output D6,
  output D7
);

  wire and_1_out, and_2_out, and_3_out, and_4_out, and_5_out, and_6_out, and_7_out, and_8_out, and_9_out,
       and_10_out, and_11_out, and_12_out, and_13_out, and_14_out, and_15_out, and_16_out, and_17_out,
       and_18_out, and_19_out, and_20_out, and_21_out, and_22_out, and_23_out, and_24_out, and_25_out,
       and_26_out, and_27_out, and_28_out, and_29_out, and_30_out, and_31_out, and_32_out, and_33_out,
       and_34_out, and_35_out, and_36_out, and_37_out, and_38_out, and_39_out, and_40_out, and_41_out,
       and_42_out, and_43_out, and_44_out, and_45_out, and_46_out, and_47_out, and_48_out, and_49_out,
       and_50_out, and_51_out, and_52_out, and_53_out, and_54_out, and_55_out, and_56_out, and_57_out,
       and_58_out, and_59_out, and_60_out, and_61_out, and_62_out, and_63_out, and_64_out, and_65_out,
       and_66_out, and_67_out, and_68_out, and_69_out, and_70_out, and_71_out, and_72_out, and_73_out,
       and_74_out, and_75_out, and_76_out, and_77_out, and_78_out, and_79_out, and_80_out, and_81_out,
       and_82_out, and_83_out, and_84_out, and_85_out, and_86_out, and_87_out, and_88_out, and_89_out,
       and_90_out, and_91_out, and_92_out, and_93_out, and_94_out, and_95_out, and_96_out, and_97_out,
       and_98_out, and_99_out, and_100_out, and_101_out, and_102_out, not_1_out, not_2_out, not_3_out,
       not_4_out, not_5_out, not_6_out, not_7_out, not_8_out, not_9_out, not_10_out, not_11_out, not_12_out,
       not_13_out, not_14_out, not_15_out, not_16_out, not_17_out, not_18_out, not_19_out, not_20_out,
       not_21_out, not_22_out, not_23_out, not_24_out, not_25_out, not_26_out, not_27_out, not_28_out,
       not_29_out, not_30_out, not_31_out, not_32_out, not_33_out, not_34_out, not_35_out, not_36_out,
       not_37_out, not_38_out, not_39_out, not_40_out, not_41_out, not_42_out, not_43_out, not_44_out,
       not_45_out, not_46_out, not_47_out, not_48_out, not_49_out, not_50_out, not_51_out, not_52_out,
       not_53_out, not_54_out, not_55_out, not_56_out, not_57_out, not_58_out, not_59_out, not_60_out,
       not_61_out, not_62_out, not_63_out, not_64_out, not_65_out, not_66_out, not_67_out, not_68_out,
       not_69_out, not_70_out, not_71_out, not_72_out, not_73_out, not_74_out, not_75_out, not_76_out,
       not_77_out, not_78_out, not_79_out, not_80_out, not_81_out, not_82_out, not_83_out, not_84_out,
       not_85_out, not_86_out, not_87_out, not_88_out, not_89_out, not_90_out, not_91_out, not_92_out,
       not_93_out, not_94_out, not_95_out, not_96_out, not_97_out, not_98_out, not_99_out, not_100_out,
       not_101_out, not_102_out, not_103_out, not_104_out, not_105_out, not_106_out, not_107_out,
       not_108_out, not_109_out, not_110_out, not_111_out, not_112_out, not_113_out, not_114_out,
       not_115_out, not_116_out, not_117_out, not_118_out, not_119_out, not_120_out, not_121_out,
       not_122_out, not_123_out, not_124_out, not_125_out, not_126_out, not_127_out, not_128_out,
       not_129_out, not_130_out, not_131_out, not_132_out, not_133_out, not_134_out, not_135_out,
       not_136_out, not_137_out, not_138_out, not_139_out, not_140_out, not_141_out, not_142_out,
       not_143_out, not_144_out, not_145_out, not_146_out, not_147_out, not_148_out, not_149_out,
       not_150_out, not_151_out, not_152_out, not_153_out, not_154_out, not_155_out, not_156_out,
       not_157_out, not_158_out, not_159_out, not_160_out, not_161_out, not_162_out, not_163_out,
       not_164_out, not_165_out, not_166_out, not_167_out, not_168_out, not_169_out, not_170_out,
       not_171_out, not_172_out, not_173_out, not_174_out, not_175_out, not_176_out, not_177_out,
       not_178_out, not_179_out, not_180_out, not_181_out, not_182_out, not_183_out, not_184_out,
       not_185_out, not_186_out, not_187_out, not_188_out, not_189_out, not_190_out, not_191_out,
       not_192_out, not_193_out, not_194_out, not_195_out, not_196_out, not_197_out, not_198_out,
       not_199_out, not_200_out, not_201_out, not_202_out, not_203_out, not_204_out, not_205_out,
       not_206_out, not_207_out, not_208_out, not_209_out, not_210_out, not_211_out, not_212_out,
       not_213_out, not_214_out, not_215_out, not_216_out, not_217_out, not_218_out, not_219_out,
       not_220_out, not_221_out, not_222_out, not_223_out, not_224_out;

  not not_1 (not_1_out, B);
  not not_2 (not_2_out, C);
  not not_3 (not_3_out, E);
  not not_4 (not_4_out, A);
  not not_5 (not_5_out, B);
  not not_6 (not_6_out, D);
  not not_7 (not_7_out, F);
  not not_8 (not_8_out, B);
  not not_9 (not_9_out, C);
  not not_10 (not_10_out, B);
  not not_11 (not_11_out, C);
  not not_12 (not_12_out, C);
  not not_13 (not_13_out, A);
  not not_14 (not_14_out, B);
  not not_15 (not_15_out, E);
  not not_16 (not_16_out, A);
  not not_17 (not_17_out, E);
  not not_18 (not_18_out, C);
  not not_19 (not_19_out, D);
  not not_20 (not_20_out, F);
  not not_21 (not_21_out, A);
  not not_22 (not_22_out, D);
  not not_23 (not_23_out, D);
  not not_24 (not_24_out, E);
  not not_25 (not_25_out, A);
  not not_26 (not_26_out, F);
  not not_27 (not_27_out, E);
  not not_28 (not_28_out, F);
  not not_29 (not_29_out, D);
  not not_30 (not_30_out, E);
  not not_31 (not_31_out, F);
  not not_32 (not_32_out, A);
  not not_33 (not_33_out, C);
  not not_34 (not_34_out, E);
  not not_35 (not_35_out, F);
  not not_36 (not_36_out, A);
  not not_37 (not_37_out, B);
  not not_38 (not_38_out, C);
  not not_39 (not_39_out, E);
  not not_40 (not_40_out, B);
  not not_41 (not_41_out, C);
  not not_42 (not_42_out, F);
  not not_43 (not_43_out, A);
  not not_44 (not_44_out, D);
  not not_45 (not_45_out, E);
  not not_46 (not_46_out, A);
  not not_47 (not_47_out, F);
  not not_48 (not_48_out, A);
  not not_49 (not_49_out, B);
  not not_50 (not_50_out, D);
  not not_51 (not_51_out, F);
  not not_52 (not_52_out, A);
  not not_53 (not_53_out, C);
  not not_54 (not_54_out, D);
  not not_55 (not_55_out, A);
  not not_56 (not_56_out, E);
  not not_57 (not_57_out, B);
  not not_58 (not_58_out, C);
  not not_59 (not_59_out, B);
  not not_60 (not_60_out, F);
  not not_61 (not_61_out, C);
  not not_62 (not_62_out, E);
  not not_63 (not_63_out, F);
  not not_64 (not_64_out, B);
  not not_65 (not_65_out, E);
  not not_66 (not_66_out, C);
  not not_67 (not_67_out, D);
  not not_68 (not_68_out, E);
  not not_69 (not_69_out, D);
  not not_70 (not_70_out, A);
  not not_71 (not_71_out, B);
  not not_72 (not_72_out, D);
  not not_73 (not_73_out, A);
  not not_74 (not_74_out, B);
  not not_75 (not_75_out, E);
  not not_76 (not_76_out, F);
  not not_77 (not_77_out, B);
  not not_78 (not_78_out, D);
  not not_79 (not_79_out, E);
  not not_80 (not_80_out, A);
  not not_81 (not_81_out, C);
  not not_82 (not_82_out, D);
  not not_83 (not_83_out, A);
  not not_84 (not_84_out, C);
  not not_85 (not_85_out, D);
  not not_86 (not_86_out, A);
  not not_87 (not_87_out, C);
  not not_88 (not_88_out, A);
  not not_89 (not_89_out, D);
  not not_90 (not_90_out, A);
  not not_91 (not_91_out, B);
  not not_92 (not_92_out, E);
  not not_93 (not_93_out, A);
  not not_94 (not_94_out, B);
  not not_95 (not_95_out, F);
  not not_96 (not_96_out, A);
  not not_97 (not_97_out, E);
  not not_98 (not_98_out, F);
  not not_99 (not_99_out, B);
  not not_100 (not_100_out, E);
  not not_101 (not_101_out, F);
  not not_102 (not_102_out, A);
  not not_103 (not_103_out, E);
  not not_104 (not_104_out, D);
  not not_105 (not_105_out, E);
  not not_106 (not_106_out, C);
  not not_107 (not_107_out, F);
  not not_108 (not_108_out, B);
  not not_109 (not_109_out, C);
  not not_110 (not_110_out, D);
  not not_111 (not_111_out, C);
  not not_112 (not_112_out, D);
  not not_113 (not_113_out, A);
  not not_114 (not_114_out, C);
  not not_115 (not_115_out, D);
  not not_116 (not_116_out, A);
  not not_117 (not_117_out, B);
  not not_118 (not_118_out, E);
  not not_119 (not_119_out, B);
  not not_120 (not_120_out, F);
  not not_121 (not_121_out, A);
  not not_122 (not_122_out, E);
  not not_123 (not_123_out, A);
  not not_124 (not_124_out, B);
  not not_125 (not_125_out, B);
  not not_126 (not_126_out, E);
  not not_127 (not_127_out, A);
  not not_128 (not_128_out, D);
  not not_129 (not_129_out, F);
  not not_130 (not_130_out, D);
  not not_131 (not_131_out, E);
  not not_132 (not_132_out, F);
  not not_133 (not_133_out, C);
  not not_134 (not_134_out, B);
  not not_135 (not_135_out, C);
  not not_136 (not_136_out, D);
  not not_137 (not_137_out, B);
  not not_138 (not_138_out, C);
  not not_139 (not_139_out, D);
  not not_140 (not_140_out, C);
  not not_141 (not_141_out, E);
  not not_142 (not_142_out, A);
  not not_143 (not_143_out, B);
  not not_144 (not_144_out, D);
  not not_145 (not_145_out, F);
  not not_146 (not_146_out, B);
  not not_147 (not_147_out, C);
  not not_148 (not_148_out, F);
  not not_149 (not_149_out, A);
  not not_150 (not_150_out, B);
  not not_151 (not_151_out, E);
  not not_152 (not_152_out, F);
  not not_153 (not_153_out, A);
  not not_154 (not_154_out, C);
  not not_155 (not_155_out, F);
  not not_156 (not_156_out, D);
  not not_157 (not_157_out, F);
  not not_158 (not_158_out, F);
  not not_159 (not_159_out, C);
  not not_160 (not_160_out, E);
  not not_161 (not_161_out, F);
  not not_162 (not_162_out, D);
  not not_163 (not_163_out, F);
  not not_164 (not_164_out, F);
  not not_165 (not_165_out, A);
  not not_166 (not_166_out, C);
  not not_167 (not_167_out, E);
  not not_168 (not_168_out, A);
  not not_169 (not_169_out, D);
  not not_170 (not_170_out, E);
  not not_171 (not_171_out, B);
  not not_172 (not_172_out, C);
  not not_173 (not_173_out, A);
  not not_174 (not_174_out, A);
  not not_175 (not_175_out, E);
  not not_176 (not_176_out, D);
  not not_177 (not_177_out, C);
  not not_178 (not_178_out, B);
  not not_179 (not_179_out, E);
  not not_180 (not_180_out, A);
  not not_181 (not_181_out, B);
  not not_182 (not_182_out, D);
  not not_183 (not_183_out, F);
  not not_184 (not_184_out, A);
  not not_185 (not_185_out, B);
  not not_186 (not_186_out, C);
  not not_187 (not_187_out, D);
  not not_188 (not_188_out, A);
  not not_189 (not_189_out, B);
  not not_190 (not_190_out, E);
  not not_191 (not_191_out, B);
  not not_192 (not_192_out, C);
  not not_193 (not_193_out, F);
  not not_194 (not_194_out, A);
  not not_195 (not_195_out, B);
  not not_196 (not_196_out, E);
  not not_197 (not_197_out, F);
  not not_198 (not_198_out, A);
  not not_199 (not_199_out, B);
  not not_200 (not_200_out, B);
  not not_201 (not_201_out, E);
  not not_202 (not_202_out, A);
  not not_203 (not_203_out, C);
  not not_204 (not_204_out, F);
  not not_205 (not_205_out, D);
  not not_206 (not_206_out, F);
  not not_207 (not_207_out, A);
  not not_208 (not_208_out, C);
  not not_209 (not_209_out, A);
  not not_210 (not_210_out, D);
  not not_211 (not_211_out, E);
  not not_212 (not_212_out, F);
  not not_213 (not_213_out, C);
  not not_214 (not_214_out, E);
  not not_215 (not_215_out, F);
  not not_216 (not_216_out, B);
  not not_217 (not_217_out, C);
  not not_218 (not_218_out, D);
  not not_219 (not_219_out, D);
  not not_220 (not_220_out, F);
  not not_221 (not_221_out, B);
  not not_222 (not_222_out, D);
  not not_223 (not_223_out, F);
  not not_224 (not_224_out, C);
  and and_1 (and_1_out, not_1_out, D, F);
  and and_2 (and_2_out, A, not_2_out, not_3_out);
  and and_3 (and_3_out, A, C, E);
  and and_4 (and_4_out, not_4_out, not_5_out, not_6_out, not_7_out);
  and and_5 (and_5_out, not_8_out, not_9_out, E, F);
  and and_6 (and_6_out, not_10_out, not_11_out, D, E);
  and and_7 (and_7_out, not_12_out, D, E, F);
  and and_8 (and_8_out, not_13_out, not_14_out, C, not_15_out);
  and and_9 (and_9_out, not_16_out, C, not_17_out, F);
  and and_10 (and_10_out, B, not_18_out, not_19_out, not_20_out);
  and and_11 (and_11_out, not_21_out, B, not_22_out, F);
  and and_12 (and_12_out, B, not_23_out, not_24_out, F);
  and and_13 (and_13_out, not_25_out, B, E, not_26_out);
  and and_14 (and_14_out, B, D, not_27_out, not_28_out);
  and and_15 (and_15_out, A, not_29_out, not_30_out, not_31_out);
  and and_16 (and_16_out, not_32_out, not_33_out, not_34_out, not_35_out);
  and and_17 (and_17_out, not_36_out, not_37_out, not_38_out, D, not_39_out);
  and and_18 (and_18_out, not_40_out, not_41_out, D, not_42_out);
  and and_19 (and_19_out, not_43_out, C, not_44_out, not_45_out);
  and and_20 (and_20_out, not_46_out, C, E, not_47_out);
  and and_21 (and_21_out, not_48_out, not_49_out, C, D, E);
  and and_22 (and_22_out, B, not_50_out, not_51_out);
  and and_23 (and_23_out, not_52_out, B, not_53_out, not_54_out, E);
  and and_24 (and_24_out, not_55_out, B, C, not_56_out);
  and and_25 (and_25_out, A, not_57_out, not_58_out, E);
  and and_26 (and_26_out, A, not_59_out, D, not_60_out);
  and and_27 (and_27_out, A, not_61_out, D, E);
  and and_28 (and_28_out, A, C, not_62_out, not_63_out);
  and and_29 (and_29_out, A, not_64_out, C, D, not_65_out);
  and and_30 (and_30_out, A, B, not_66_out, not_67_out, not_68_out);
  and and_31 (and_31_out, A, B, C, not_69_out, E);
  and and_32 (and_32_out, not_70_out, not_71_out, not_72_out);
  and and_33 (and_33_out, not_73_out, not_74_out, not_75_out, not_76_out);
  and and_34 (and_34_out, not_77_out, not_78_out, not_79_out);
  and and_35 (and_35_out, not_80_out, not_81_out, not_82_out, F);
  and and_36 (and_36_out, not_83_out, not_84_out, not_85_out, E);
  and and_37 (and_37_out, not_86_out, not_87_out, E, F);
  and and_38 (and_38_out, not_88_out, not_89_out, E, F);
  and and_39 (and_39_out, not_90_out, not_91_out, C, not_92_out);
  and and_40 (and_40_out, not_93_out, not_94_out, C, not_95_out);
  and and_41 (and_41_out, not_96_out, C, not_97_out, not_98_out);
  and and_42 (and_42_out, not_99_out, C, not_100_out, not_101_out);
  and and_43 (and_43_out, not_102_out, B, D);
  and and_44 (and_44_out, B, D, not_103_out);
  and and_45 (and_45_out, B, C, D);
  and and_46 (and_46_out, A, not_104_out, not_105_out, F);
  and and_47 (and_47_out, A, not_106_out, E, not_107_out);
  and and_48 (and_48_out, A, not_108_out, not_109_out, D, F);
  and and_49 (and_49_out, A, C, not_110_out, E);
  and and_50 (and_50_out, A, C, E, F);
  and and_51 (and_51_out, A, B, not_111_out, not_112_out);
  and and_52 (and_52_out, not_113_out, not_114_out, not_115_out, E);
  and and_53 (and_53_out, not_116_out, not_117_out, D, not_118_out);
  and and_54 (and_54_out, not_119_out, D, not_120_out);
  and and_55 (and_55_out, not_121_out, C, not_122_out);
  and and_56 (and_56_out, not_123_out, not_124_out, C, D);
  and and_57 (and_57_out, not_125_out, C, D, not_126_out);
  and and_58 (and_58_out, not_127_out, B, not_128_out, not_129_out);
  and and_59 (and_59_out, B, not_130_out, not_131_out, not_132_out);
  and and_60 (and_60_out, B, not_133_out, D, E);
  and and_61 (and_61_out, A, not_134_out, not_135_out, not_136_out);
  and and_62 (and_62_out, A, not_137_out, not_138_out, E);
  and and_63 (and_63_out, A, C, not_139_out, E);
  and and_64 (and_64_out, A, B, not_140_out, not_141_out);
  and and_65 (and_65_out, A, B, C, E);
  and and_66 (and_66_out, not_142_out, not_143_out, not_144_out, not_145_out);
  and and_67 (and_67_out, not_146_out, not_147_out, D, E, not_148_out);
  and and_68 (and_68_out, not_149_out, not_150_out, C, not_151_out, not_152_out);
  and and_69 (and_69_out, not_153_out, B, not_154_out, not_155_out);
  and and_70 (and_70_out, B, not_156_out, E, not_157_out);
  and and_71 (and_71_out, B, C, D, not_158_out);
  and and_72 (and_72_out, A, not_159_out, not_160_out, not_161_out);
  and and_73 (and_73_out, A, C, not_162_out, not_163_out);
  and and_74 (and_74_out, A, C, E, not_164_out);
  and and_75 (and_75_out, not_165_out, not_166_out, not_167_out);
  and and_76 (and_76_out, not_168_out, not_169_out, not_170_out);
  and and_77 (and_77_out, not_171_out, not_172_out, D);
  and and_78 (and_78_out, not_173_out, C, E);
  and and_79 (and_79_out, not_174_out, B, not_175_out);
  and and_80 (and_80_out, B, not_176_out);
  and and_81 (and_81_out, A, not_177_out, E);
  and and_82 (and_82_out, A, not_178_out, D);
  and and_83 (and_83_out, A, C, not_179_out);
  and and_84 (and_84_out, not_180_out, not_181_out, not_182_out, not_183_out);
  and and_85 (and_85_out, not_184_out, not_185_out, not_186_out, not_187_out, E);
  and and_86 (and_86_out, not_188_out, not_189_out, D, not_190_out, F);
  and and_87 (and_87_out, not_191_out, not_192_out, D, E, not_193_out);
  and and_88 (and_88_out, not_194_out, not_195_out, C, not_196_out, not_197_out);
  and and_89 (and_89_out, not_198_out, not_199_out, C, D, F);
  and and_90 (and_90_out, not_200_out, C, D, not_201_out, F);
  and and_91 (and_91_out, not_202_out, B, not_203_out, not_204_out);
  and and_92 (and_92_out, B, not_205_out, E, not_206_out);
  and and_93 (and_93_out, not_207_out, B, not_208_out, D, E);
  and and_94 (and_94_out, not_209_out, B, C, not_210_out, not_211_out, F);
  and and_95 (and_95_out, B, C, D, not_212_out);
  and and_96 (and_96_out, A, not_213_out, not_214_out, not_215_out);
  and and_97 (and_97_out, A, not_216_out, not_217_out, not_218_out, F);
  and and_98 (and_98_out, A, C, not_219_out, not_220_out);
  and and_99 (and_99_out, A, not_221_out, C, not_222_out, E);
  and and_100 (and_100_out, A, C, E, not_223_out);
  and and_101 (and_101_out, A, B, not_224_out, D, F);
  and and_102 (and_102_out, A, B, C, D, E);
  or or_1 (D5, and_66_out, and_67_out, and_68_out, and_69_out, and_70_out, and_71_out, and_72_out, and_73_out, and_74_out);
  or or_2 (D6, and_75_out, and_76_out, F, and_77_out, and_78_out, and_79_out, and_80_out, and_81_out, and_82_out, and_83_out);
  or or_3 (D1, and_1_out, and_2_out, and_3_out, and_4_out, and_5_out, and_6_out, and_7_out, and_8_out, and_9_out, and_10_out, and_11_out, and_12_out, and_13_out, and_14_out, and_15_out);
  or or_4 (D2, and_16_out, and_17_out, and_18_out, and_19_out, and_20_out, and_21_out, and_22_out, and_23_out, and_24_out, and_25_out, and_26_out, and_27_out, and_28_out, and_29_out, and_30_out, and_31_out);
  or or_5 (D3, and_32_out, and_33_out, and_34_out, and_35_out, and_36_out, and_37_out, and_38_out, and_39_out, and_40_out, and_41_out, and_42_out, and_43_out, and_44_out, and_45_out, and_46_out, and_47_out, and_48_out, and_49_out, and_50_out, and_51_out);
  or or_6 (D4, and_52_out, and_53_out, and_54_out, and_55_out, and_56_out, and_57_out, and_58_out, and_59_out, and_60_out, and_61_out, and_62_out, and_63_out, and_64_out, and_65_out);
  or or_7 (D7, and_84_out, and_85_out, and_86_out, and_87_out, and_88_out, and_89_out, and_90_out, and_91_out, and_92_out, and_93_out, and_94_out, and_95_out, and_96_out, and_97_out, and_98_out, and_99_out, and_100_out, and_101_out, and_102_out);
endmodule

module Display_2 (
  input  A,
  input  B,
  input  C,
  input  D,
  input  E,
  input  F,
  output D8,
  output D9,
  output D10,
  output D11,
  output D12,
  output D13,
  output D14
);

  wire and_1_out, and_2_out, and_3_out, and_4_out, and_5_out, and_6_out, and_7_out, and_8_out, and_9_out,
       and_10_out, and_11_out, and_12_out, and_13_out, and_14_out, and_15_out, and_16_out, and_17_out,
       and_18_out, and_19_out, and_20_out, and_21_out, and_22_out, and_23_out, and_24_out, and_25_out,
       not_1_out, not_2_out, not_3_out, not_4_out, not_5_out, not_6_out, not_7_out, not_8_out, not_9_out,
       not_10_out, not_11_out, not_12_out, not_13_out, not_14_out, not_15_out, not_16_out, not_17_out,
       not_18_out, not_19_out, not_20_out, not_21_out, not_22_out, not_23_out, not_24_out, not_25_out,
       not_26_out, not_27_out, not_28_out, not_29_out, not_30_out, not_31_out, not_32_out, not_33_out,
       not_34_out, not_35_out, not_36_out, not_37_out, not_38_out, not_39_out, not_40_out, not_41_out,
       not_42_out, not_43_out, not_44_out;

  not not_1 (not_1_out, A);
  not not_2 (not_2_out, B);
  not not_3 (not_3_out, D);
  not not_4 (not_4_out, E);
  not not_5 (not_5_out, B);
  not not_6 (not_6_out, C);
  not not_7 (not_7_out, C);
  not not_8 (not_8_out, C);
  not not_9 (not_9_out, A);
  not not_10 (not_10_out, B);
  not not_11 (not_11_out, C);
  not not_12 (not_12_out, A);
  not not_13 (not_13_out, B);
  not not_14 (not_14_out, D);
  not not_15 (not_15_out, E);
  not not_16 (not_16_out, C);
  not not_17 (not_17_out, D);
  not not_18 (not_18_out, E);
  and and_1 (and_1_out, B, D);
  and and_2 (and_2_out, B, C);
  not not_19 (not_19_out, A);
  not not_20 (not_20_out, B);
  not not_21 (not_21_out, C);
  not not_22 (not_22_out, A);
  not not_23 (not_23_out, B);
  not not_24 (not_24_out, D);
  not not_25 (not_25_out, E);
  not not_26 (not_26_out, A);
  not not_27 (not_27_out, C);
  not not_28 (not_28_out, A);
  not not_29 (not_29_out, D);
  not not_30 (not_30_out, A);
  not not_31 (not_31_out, E);
  not not_32 (not_32_out, C);
  not not_33 (not_33_out, D);
  not not_34 (not_34_out, A);
  not not_35 (not_35_out, B);
  not not_36 (not_36_out, D);
  not not_37 (not_37_out, E);
  not not_38 (not_38_out, B);
  not not_39 (not_39_out, C);
  not not_40 (not_40_out, C);
  not not_41 (not_41_out, C);
  and and_3 (and_3_out, not_1_out, not_2_out, not_3_out, not_4_out);
  and and_4 (and_4_out, not_5_out, not_6_out);
  and and_5 (and_5_out, not_7_out, D);
  and and_6 (and_6_out, B, C);
  and and_7 (and_7_out, A, not_8_out, E);
  and and_8 (and_8_out, not_9_out, not_10_out, not_11_out);
  and and_9 (and_9_out, not_12_out, not_13_out, not_14_out, not_15_out);
  and and_10 (and_10_out, A, C);
  and and_11 (and_11_out, A, B);
  not not_42 (not_42_out, A);
  not not_43 (not_43_out, B);
  and and_12 (and_12_out, not_16_out, not_17_out, not_18_out);
  or or_1 (D11, and_1_out, and_2_out, A);
  and and_13 (and_13_out, not_19_out, not_20_out, not_21_out);
  and and_14 (and_14_out, not_22_out, not_23_out, not_24_out, not_25_out);
  and and_15 (and_15_out, not_26_out, not_27_out, D);
  and and_16 (and_16_out, not_28_out, B, C, not_29_out);
  and and_17 (and_17_out, not_30_out, B, C, not_31_out);
  and and_18 (and_18_out, A, B, C, D);
  not not_44 (not_44_out, B);
  and and_19 (and_19_out, not_32_out, not_33_out);
  and and_20 (and_20_out, C, D, E);
  and and_21 (and_21_out, not_34_out, not_35_out, not_36_out, not_37_out);
  and and_22 (and_22_out, not_38_out, not_39_out);
  and and_23 (and_23_out, not_40_out, D);
  and and_24 (and_24_out, B, C);
  and and_25 (and_25_out, A, not_41_out, E);
  or or_2 (D8, and_3_out, and_4_out, and_5_out, and_6_out, and_7_out);
  or or_3 (D9, and_8_out, and_9_out, and_10_out, and_11_out);
  or or_4 (D10, not_42_out, not_43_out, and_12_out);
  or or_5 (D12, and_13_out, and_14_out, and_15_out, and_16_out, and_17_out, and_18_out);
  or or_6 (D13, not_44_out, and_19_out, and_20_out, A);
  or or_7 (D14, and_21_out, and_22_out, and_23_out, and_24_out, and_25_out);
endmodule

module latch_D (
  input  in_1,
  input  EN,
  output MX
);

  wire nand_1_out, nand_2_out, nand_4_out, not_1_out;

  nand nand_1 (nand_1_out, in_1, EN);
  nand nand_2 (nand_2_out, EN, not_1_out);
  not not_1 (not_1_out, in_1);
  nand nand_3 (MX, nand_1_out, nand_4_out);
  nand nand_4 (nand_4_out, MX, nand_2_out);
endmodule

module memoria (
  input  in_1,
  input  in_2,
  input  in_3,
  input  in_4,
  input  in_5,
  input  in_6,
  input  in_7,
  output out_8,
  output out_9,
  output out_10,
  output out_11,
  output out_12,
  output out_13
);

  D_Flip_Flop #(.trigger("falling")) d_ff_1 (.clk(in_1), .D(in_2), .Q(out_8));  // open: Qn, preset, en, reset
  D_Flip_Flop #(.trigger("falling")) d_ff_2 (.clk(in_1), .D(in_3), .Q(out_9));  // open: Qn, preset, en, reset
  D_Flip_Flop #(.trigger("falling")) d_ff_3 (.clk(in_1), .D(in_4), .Q(out_10));  // open: Qn, preset, en, reset
  D_Flip_Flop #(.trigger("falling")) d_ff_4 (.clk(in_1), .D(in_5), .Q(out_11));  // open: Qn, preset, en, reset
  D_Flip_Flop #(.trigger("falling")) d_ff_5 (.clk(in_1), .D(in_6), .Q(out_12));  // open: Qn, preset, en, reset
  D_Flip_Flop #(.trigger("falling")) d_ff_6 (.clk(in_1), .D(in_7), .Q(out_13));  // open: Qn, preset, en, reset
endmodule

// Enable
module enable (
  input  in_1,
  input  in_2,
  input  in_3,
  input  in_4,
  input  in_5,
  input  in_6,
  output out_7
);

  or or_1 (out_7, in_1, in_2, in_3, in_4, in_5, in_6);
endmodule

module memoria_2 (
  input  in_1,
  input  in_2,
  input  in_3,
  input  in_4,
  output out_5,
  output out_6,
  output out_7
);

  D_Flip_Flop #(.trigger("falling")) d_ff_1 (.clk(in_1), .D(in_2), .Q(out_5));  // open: Qn, preset, en, reset
  D_Flip_Flop #(.trigger("falling")) d_ff_2 (.clk(in_1), .D(in_3), .Q(out_6));  // open: Qn, preset, en, reset
  D_Flip_Flop #(.trigger("falling")) d_ff_3 (.clk(in_1), .D(in_4), .Q(out_7));  // open: Qn, preset, en, reset
endmodule

module Latch_D_2 (
  input  in_1,
  input  EN,
  output MX
);

  wire nand_1_out, nand_2_out, nand_4_out, not_1_out;

  nand nand_1 (nand_1_out, in_1, EN);
  nand nand_2 (nand_2_out, EN, not_1_out);
  not not_1 (not_1_out, in_1);
  nand nand_3 (MX, nand_1_out, nand_4_out);
  nand nand_4 (nand_4_out, MX, nand_2_out);
endmodule

module Multiplexador (
  input  in_1,
  input  in_2,
  input  in_3,
  output out_4
);

  wire and_1_out, and_2_out, not_1_out;

  and and_1 (and_1_out, in_1, not_1_out);
  not not_1 (not_1_out, in_3);
  and and_2 (and_2_out, in_2, in_3);
  or or_1 (out_4, and_1_out, and_2_out);
endmodule

module multiplexador_6_bits (
  input  in_1,
  input  in_2,
  input  in_3,
  input  in_4,
  input  in_5,
  input  in_6,
  input  in_7,
  output out_8,
  output out_9,
  output out_10,
  output out_11,
  output out_12,
  output out_13
);

  // Multiplexador multiplexador_1: pin names not known; wires that end beside it: in_1, 1'b0, in_7, out_8
  // Multiplexador multiplexador_2: pin names not known; wires that end beside it: in_2, 1'b0, in_7, out_9
  // Multiplexador multiplexador_3: pin names not known; wires that end beside it: in_3, 1'b0, in_7, out_10
  // Multiplexador multiplexador_4: pin names not known; wires that end beside it: in_4, 1'b0, in_7, out_11
  // Multiplexador multiplexador_5: pin names not known; wires that end beside it: in_5, 1'b0, in_7, out_12
  // Multiplexador multiplexador_6: pin names not known; wires that end beside it: in_6, 1'b0, in_7, out_13
endmodule

module flipflop_D (
  input  in_1,
  input  in_2,
  output out_3
);

  wire nand_1_out, nand_2_out, nand_3_out, nand_4_out, nand_5_out, nand_6_out, nand_8_out, not_1_out,
       not_2_out;

  not not_1 (not_1_out, in_1);
  nand nand_1 (nand_1_out, in_1, in_2);
  nand nand_2 (nand_2_out, in_2, not_1_out);
  not not_2 (not_2_out, in_2);
  nand nand_3 (nand_3_out, nand_1_out, nand_4_out);
  nand nand_4 (nand_4_out, nand_3_out, nand_2_out);
  nand nand_5 (nand_5_out, nand_3_out, not_2_out);
  nand nand_6 (nand_6_out, not_2_out, nand_4_out);
  nand nand_7 (out_3, nand_5_out, nand_8_out);
  nand nand_8 (nand_8_out, out_3, nand_6_out);
endmodule

module subtrador_da_ula (
  input  B0,
  input  M0,
  input  B1,
  input  M1,
  input  B2,
  input  M2,
  input  M3,
  input  M4,
  input  M5,
  output out_10,
  output out_11,
  output out_12,
  output out_13,
  output out_14,
  output out_15
);

  wire not_1_out, not_2_out, not_3_out, somador_completo_1_out_5, somador_completo_2_out_5,
       somador_completo_3_out_5, somador_completo_4_out_5, somador_completo_5_out_5, somador_completo_6_out_5;

  not not_1 (not_1_out, B0);
  not not_2 (not_2_out, B1);
  not not_3 (not_3_out, B2);
  somador_completo somador_completo_1 (
    .in_1(not_1_out), .in_2(M0), .in_3(1'b1), .out_4(out_10), .out_5(somador_completo_1_out_5));
  somador_completo somador_completo_2 (
    .in_1(not_2_out), .in_2(M1), .in_3(somador_completo_1_out_5), .out_4(out_11),
    .out_5(somador_completo_2_out_5));
  somador_completo somador_completo_3 (
    .in_1(not_3_out), .in_2(M2), .in_3(somador_completo_2_out_5), .out_4(out_12),
    .out_5(somador_completo_3_out_5));
  somador_completo somador_completo_4 (
    .in_1(1'b1), .in_2(M3), .in_3(somador_completo_3_out_5), .out_4(out_13), .out_5(somador_completo_4_out_5));
  somador_completo somador_completo_5 (
    .in_1(1'b1), .in_2(M4), .in_3(somador_completo_4_out_5), .out_4(out_14), .out_5(somador_completo_5_out_5));
  somador_completo somador_completo_6 (
    .in_1(1'b1), .in_2(M5), .in_3(somador_completo_5_out_5), .out_4(out_15), .out_5(somador_completo_6_out_5));
endmodule

module somador_da_ula (
  input  B0,
  input  M0,
  input  B1,
  input  M1,
  input  B2,
  input  M2,
  input  M3,
  input  M4,
  input  M5,
  output out_10,
  output out_11,
  output out_12,
  output out_13,
  output out_14,
  output out_15
);

  wire somador_completo_1_out_5, somador_completo_2_out_5, somador_completo_3_out_5,
       somador_completo_4_out_5, somador_completo_5_out_5, somador_completo_6_out_5;

  somador_completo somador_completo_1 (
    .in_1(B0), .in_2(M0), .in_3(1'b0), .out_4(out_10), .out_5(somador_completo_1_out_5));
  somador_completo somador_completo_2 (
    .in_1(B1), .in_2(M1), .in_3(somador_completo_1_out_5), .out_4(out_11), .out_5(somador_completo_2_out_5));
  somador_completo somador_completo_3 (
    .in_1(B2), .in_2(M2), .in_3(somador_completo_2_out_5), .out_4(out_12), .out_5(somador_completo_3_out_5));
  somador_completo somador_completo_4 (
    .in_1(1'b0), .in_2(M3), .in_3(somador_completo_3_out_5), .out_4(out_13), .out_5(somador_completo_4_out_5));
  somador_completo somador_completo_5 (
    .in_1(1'b0), .in_2(M4), .in_3(somador_completo_4_out_5), .out_4(out_14), .out_5(somador_completo_5_out_5));
  somador_completo somador_completo_6 (
    .in_1(1'b0), .in_2(M5), .in_3(somador_completo_5_out_5), .out_4(out_15), .out_5(somador_completo_6_out_5));
endmodule

module luz_apito_final (
  input  A,
  input  B,
  input  C,
  input  D,
  input  E,
  input  F,
  output S
);

  wire and_1_out, and_2_out, and_3_out;

  and and_1 (and_1_out, A, B, E, F);
  and and_2 (and_2_out, A, B, D);
  and and_3 (and_3_out, A, B, C);
  or or_1 (S, and_1_out, and_2_out, and_3_out);
endmodule
